// Logisim project Sagui_v0.1.circ as structural Verilog: 6 circuits, main circuit main
module main (
  input  in_1
);

  wire and_1_out, and_2_out, BRANCHimm, BRANCHreg, CLK, JMPimm, JMPreg, MEMrd, MEMtoREG, MEMwr, MoveHL,
       nor_1_out, nor_2_out, or_1_out, RaZero, REGWrite, SELHL;
  wire [1:0] multiplexer_1_out;
  wire [2:0] ALUsrc;
  wire [3:0] Imm;
  wire [7:0] adder_1_out, adder_2_out, bancoreg_1_r_ra, bit_extender_1_out, movehighlowbox_1_move_high,
       movehighlowbox_1_move_low, multiplexer_2_out, multiplexer_3_out, multiplexer_4_out, multiplexer_5_out,
       multiplexer_6_out, PC, ram_2_dout, Rrb, \ula_1_saída_ula ;
  wire [7:4] ram_1_dout;
  wire [15:13] rom_1_data;
  wire [31:0] REGS;

  RAM #(.asyncread("true")) ram_1 (.addr(PC), .we(1'b0), .oe(1'b1), .clk(CLK), .dout({ram_1_dout, Imm}));  // open: din
  Register register_1 (.D(multiplexer_4_out), .en(1'b1), .clk(CLK), .Q(PC), .clr(in_1));
  // Probe on PC
  // Probe on PC
  // Probe on REGS[7:0]
  // Probe on REGS[7:0]
  // Probe on REGS[15:8]
  // Probe on REGS[15:8]
  // Probe on REGS[23:16]
  // Probe on REGS[23:16]
  // Probe on REGS[31:24]
  // Probe on REGS[31:24]
  Clock clock_1 (.out(CLK));
  // Probe on PC
  // Probe on REGS[7:0]
  // Probe on REGS[15:8]
  // Probe on REGS[23:16]
  // Probe on REGS[31:24]
  Adder adder_1 (.a(PC), .b(8'h1), .out(adder_1_out));  // open: cin, cout
  and and_1 (and_1_out, BRANCHreg, RaZero);
  nor nor_1 (nor_1_out, JMPreg, and_1_out);
  assign bit_extender_1_out = {{4{1'b0}}, Imm};  // Bit_Extender bit_extender_1
  and and_2 (and_2_out, BRANCHimm, RaZero);
  or or_1 (or_1_out, MoveHL, BRANCHimm);
  Adder adder_2 (.a(PC), .b(bit_extender_1_out), .out(adder_2_out));  // open: cin, cout
  Multiplexer #(.enable("false"), .width(2)) multiplexer_1 (
    .in0(Imm[3:2]), .in1(2'b00), .out(multiplexer_1_out), .sel(or_1_out));
  Multiplexer #(.enable("false"), .width(8)) multiplexer_2 (
    .in0(adder_2_out), .in1(adder_1_out), .out(multiplexer_2_out), .sel(nor_2_out));
  nor nor_2 (nor_2_out, JMPimm, and_2_out);
  Multiplexer #(.enable("false"), .width(8)) multiplexer_3 (
    .in0(multiplexer_6_out), .in1(multiplexer_5_out), .out(multiplexer_3_out), .sel(MoveHL));
  Multiplexer #(.enable("false"), .width(8)) multiplexer_4 (
    .in0(Rrb), .in1(multiplexer_2_out), .out(multiplexer_4_out), .sel(nor_1_out));
  Multiplexer #(.enable("false"), .width(8)) multiplexer_5 (
    .in0(movehighlowbox_1_move_low), .in1(movehighlowbox_1_move_high), .out(multiplexer_5_out), .sel(SELHL));
  BancoReg bancoreg_1 (
    .R_0(REGS[7:0]), .R_1(REGS[15:8]), .R_2(REGS[23:16]), .R_3(REGS[31:24]), .R_ra(bancoreg_1_r_ra),
    .R_rb(Rrb), .WriteRegister(multiplexer_1_out), .in_1(multiplexer_3_out), .RegWrite(REGWrite), .CLK(CLK),
    .ResetGeral(in_1), .SELra(multiplexer_1_out), .SELrb(Imm[1:0]));
  MoveHighLowBox movehighlowbox_1 (
    .Move_HIGH(movehighlowbox_1_move_high), .Move_LOW(movehighlowbox_1_move_low), .Imm(Imm),
    .in_2(bancoreg_1_r_ra));
  ROM #(.addrWidth(4), .dataWidth(16)) rom_1 (
    .addr(ram_1_dout),
    .data({rom_1_data, REGWrite, SELHL, MoveHL, BRANCHimm, BRANCHreg, JMPimm, JMPreg, MEMtoREG, MEMrd, MEMwr, ALUsrc}));
  ULA ula_1 (
    .\Saída_ULA (\ula_1_saída_ula ), .R_ra_____0(RaZero), .in_1(bancoreg_1_r_ra), .in_2(Rrb), .ULA_src(ALUsrc));
  Multiplexer #(.enable("false"), .width(8)) multiplexer_6 (
    .in0(\ula_1_saída_ula ), .in1(ram_2_dout), .out(multiplexer_6_out), .sel(MEMtoREG));
  RAM #(.asyncread("true")) ram_2 (
    .addr(Rrb), .we(MEMwr), .oe(MEMrd), .clk(CLK), .din(bancoreg_1_r_ra), .dout(ram_2_dout));

  // Other names for the same wires on the sheet: ResetGeral = in_1

  // Notes on the sheet:
  //   Memória de Instruções
  //   R[0]
  //   R[1]
  //   R[2]
  //   R[3]
  //   OpCode
  //   PC
  //   PC + Imm
  //   PC + 1
  //   contents of rom_1 (hex, n*v repeats v):
  //   100 200 40 80 1030 8 1007 1c00 1400 1000 1001 1002 1003 1004 1005 1006
  //   Memória de Controle
  //   Memória de Dados
endmodule

module BancoReg (
  input  [7:0] in_1,
  input  [1:0] SELra,
  input  [1:0] WriteRegister,
  input  [1:0] SELrb,
  input  RegWrite,
  input  CLK,
  input  ResetGeral,
  output [7:0] R_0,
  output [7:0] R_ra,
  output [7:0] R_1,
  output [7:0] R_rb,
  output [7:0] R_2,
  output [7:0] R_3
);

  wire demultiplexer_2_out0, demultiplexer_2_out1, demultiplexer_2_out2, demultiplexer_2_out3;
  wire [7:0] demultiplexer_1_out0, demultiplexer_1_out1, demultiplexer_1_out2, demultiplexer_1_out3;

  Demultiplexer #(.enable("false"), .select(2), .width(8)) demultiplexer_1 (
    .out0(demultiplexer_1_out0), .out1(demultiplexer_1_out1), .out2(demultiplexer_1_out2),
    .out3(demultiplexer_1_out3), .in(in_1), .sel(WriteRegister));
  Demultiplexer #(.enable("false"), .select(2)) demultiplexer_2 (
    .out0(demultiplexer_2_out0), .out1(demultiplexer_2_out1), .out2(demultiplexer_2_out2),
    .out3(demultiplexer_2_out3), .in(RegWrite), .sel(WriteRegister));
  Register register_1 (.D(demultiplexer_1_out0), .en(demultiplexer_2_out0), .clk(CLK), .Q(R_0), .clr(ResetGeral));
  Register register_2 (.D(demultiplexer_1_out1), .en(demultiplexer_2_out1), .clk(CLK), .Q(R_1), .clr(ResetGeral));
  Register register_3 (.D(demultiplexer_1_out2), .en(demultiplexer_2_out2), .clk(CLK), .Q(R_2), .clr(ResetGeral));
  Register register_4 (.D(demultiplexer_1_out3), .en(demultiplexer_2_out3), .clk(CLK), .Q(R_3), .clr(ResetGeral));
  Multiplexer #(.enable("false"), .select(2), .width(8)) multiplexer_1 (
    .in0(R_0), .in1(R_1), .in2(R_2), .in3(R_3), .out(R_ra), .sel(SELra));
  Multiplexer #(.enable("false"), .select(2), .width(8)) multiplexer_2 (
    .in0(R_0), .in1(R_1), .in2(R_2), .in3(R_3), .out(R_rb), .sel(SELrb));

  // Notes on the sheet:
  //   (WriteData)
  //   Endereço de Escrita
  //   O que vai ser escrito no BR
  //   Banco de Registradores
  //   R0
  //   R1
  //   R2
  //   R3
  //   R[a]
  //   R[rb]
endmodule

module ULA (
  input  [7:0] in_1,
  input  [7:0] in_2,
  input  [2:0] ULA_src,
  output [7:0] \Saída_ULA ,
  output R_ra_____0
);

  wire [7:0] adder_1_out, and_1_out, lbs_1_out, not_1_out, or_1_out, rbs_1_out, subtractor_1_out;

  Adder adder_1 (.a(in_1), .b(in_2), .out(adder_1_out));  // open: cin, cout
  Subtractor subtractor_1 (.a(in_1), .b(in_2), .out(subtractor_1_out));  // open: bin, bout
  assign and_1_out = in_1 & in_2;  // AND_Gate and_1, 8 bits wide
  assign or_1_out = in_1 | in_2;  // OR_Gate or_1, 8 bits wide
  assign not_1_out = ~in_2;  // NOT_Gate not_1, 8 bits wide
  LBS lbs_1 (.Out(lbs_1_out), .in_1(in_1), .in_2(in_2));
  RBS rbs_1 (.Out(rbs_1_out), .in_1(in_1), .in_2(in_2));
  Multiplexer #(.enable("false"), .select(3), .width(8)) multiplexer_1 (
    .in0(adder_1_out), .in1(subtractor_1_out), .in2(and_1_out), .in3(or_1_out), .in4(not_1_out),
    .in5(lbs_1_out), .in6(rbs_1_out), .in7(in_2), .out(\Saída_ULA ), .sel(ULA_src));
  Comparator comparator_1 (.a(in_1), .b({8{1'b0}}), .eq(R_ra_____0));  // open: gt, lt

  // Other names for the same wires on the sheet: Rra[7:0] = in_1; Rrb[7:0] = in_2

  // Notes on the sheet:
  //   R[ra]
  //   R[rb]
  //   ULA
endmodule

module MoveHighLowBox (
  input  [3:0] Imm,
  input  [7:0] in_2,
  output [7:0] Move_HIGH,
  output [7:0] Move_LOW
);


  assign Move_HIGH = {Imm, in_2[3:0]};
  assign Move_LOW = {in_2[7:4], Imm};

  // Notes on the sheet:
  //   Registrador
endmodule

module RBS (
  input  [7:0] in_1,
  input  [7:0] in_2,
  output [7:0] Out
);

  wire multiplexer_1_out, multiplexer_2_out, multiplexer_3_out, multiplexer_4_out, multiplexer_5_out,
       multiplexer_6_out, multiplexer_7_out, multiplexer_8_out, multiplexer_9_out, multiplexer_10_out,
       multiplexer_11_out, multiplexer_12_out, multiplexer_13_out, multiplexer_14_out, multiplexer_15_out,
       multiplexer_16_out, or_1_out;
  wire [7:0] multiplexer_17_out;

  Multiplexer #(.enable("false")) multiplexer_1 (.in0(in_1[0]), .in1(in_1[1]), .out(multiplexer_1_out), .sel(in_2[0]));
  Multiplexer #(.enable("false")) multiplexer_2 (.in0(in_1[1]), .in1(in_1[2]), .out(multiplexer_2_out), .sel(in_2[0]));
  Multiplexer #(.enable("false")) multiplexer_3 (.in0(in_1[2]), .in1(in_1[3]), .out(multiplexer_3_out), .sel(in_2[0]));
  Multiplexer #(.enable("false")) multiplexer_4 (.in0(in_1[3]), .in1(in_1[4]), .out(multiplexer_4_out), .sel(in_2[0]));
  Multiplexer #(.enable("false")) multiplexer_5 (.in0(in_1[4]), .in1(in_1[5]), .out(multiplexer_5_out), .sel(in_2[0]));
  Multiplexer #(.enable("false")) multiplexer_6 (.in0(in_1[5]), .in1(in_1[6]), .out(multiplexer_6_out), .sel(in_2[0]));
  Multiplexer #(.enable("false")) multiplexer_7 (.in0(in_1[6]), .in1(in_1[7]), .out(multiplexer_7_out), .sel(in_2[0]));
  Multiplexer #(.enable("false")) multiplexer_8 (.in0(in_1[7]), .in1(1'b0), .out(multiplexer_8_out), .sel(in_2[0]));
  Multiplexer #(.enable("false")) multiplexer_9 (
    .in0(multiplexer_1_out), .in1(multiplexer_3_out), .out(multiplexer_9_out), .sel(in_2[1]));
  Multiplexer #(.enable("false")) multiplexer_10 (
    .in0(multiplexer_2_out), .in1(multiplexer_4_out), .out(multiplexer_10_out), .sel(in_2[1]));
  Multiplexer #(.enable("false")) multiplexer_11 (
    .in0(multiplexer_3_out), .in1(multiplexer_5_out), .out(multiplexer_11_out), .sel(in_2[1]));
  Multiplexer #(.enable("false")) multiplexer_12 (
    .in0(multiplexer_4_out), .in1(multiplexer_6_out), .out(multiplexer_12_out), .sel(in_2[1]));
  Multiplexer #(.enable("false")) multiplexer_13 (
    .in0(multiplexer_5_out), .in1(multiplexer_7_out), .out(multiplexer_13_out), .sel(in_2[1]));
  Multiplexer #(.enable("false")) multiplexer_14 (
    .in0(multiplexer_6_out), .in1(multiplexer_8_out), .out(multiplexer_14_out), .sel(in_2[1]));
  Multiplexer #(.enable("false")) multiplexer_15 (
    .in0(multiplexer_7_out), .in1(1'b0), .out(multiplexer_15_out), .sel(in_2[1]));
  Multiplexer #(.enable("false")) multiplexer_16 (
    .in0(multiplexer_8_out), .in1(1'b0), .out(multiplexer_16_out), .sel(in_2[1]));
  Multiplexer #(.enable("false")) multiplexer_17 (
    .in0(multiplexer_9_out), .in1(multiplexer_13_out), .out(multiplexer_17_out[0]), .sel(in_2[2]));
  Multiplexer #(.enable("false")) multiplexer_18 (
    .in0(multiplexer_10_out), .in1(multiplexer_14_out), .out(multiplexer_17_out[1]), .sel(in_2[2]));
  Multiplexer #(.enable("false")) multiplexer_19 (
    .in0(multiplexer_11_out), .in1(multiplexer_15_out), .out(multiplexer_17_out[2]), .sel(in_2[2]));
  Multiplexer #(.enable("false")) multiplexer_20 (
    .in0(multiplexer_12_out), .in1(multiplexer_16_out), .out(multiplexer_17_out[3]), .sel(in_2[2]));
  Multiplexer #(.enable("false")) multiplexer_21 (
    .in0(multiplexer_13_out), .in1(1'b0), .out(multiplexer_17_out[4]), .sel(in_2[2]));
  Multiplexer #(.enable("false")) multiplexer_22 (
    .in0(multiplexer_14_out), .in1(1'b0), .out(multiplexer_17_out[5]), .sel(in_2[2]));
  Multiplexer #(.enable("false")) multiplexer_23 (
    .in0(multiplexer_15_out), .in1(1'b0), .out(multiplexer_17_out[6]), .sel(in_2[2]));
  Multiplexer #(.enable("false")) multiplexer_24 (
    .in0(multiplexer_16_out), .in1(1'b0), .out(multiplexer_17_out[7]), .sel(in_2[2]));
  or or_1 (or_1_out, in_2[3], in_2[4], in_2[5], in_2[6], in_2[7]);
  Multiplexer #(.enable("false"), .width(8)) multiplexer_25 (
    .in0(multiplexer_17_out), .in1({8{1'b0}}), .out(Out), .sel(or_1_out));

  // Notes on the sheet:
  //   Input
  //   Shift
endmodule

module LBS (
  input  [7:0] in_1,
  input  [7:0] in_2,
  output [7:0] Out
);

  wire multiplexer_1_out, multiplexer_2_out, multiplexer_3_out, multiplexer_4_out, multiplexer_5_out,
       multiplexer_6_out, multiplexer_7_out, multiplexer_8_out, multiplexer_9_out, multiplexer_10_out,
       multiplexer_11_out, multiplexer_12_out, multiplexer_13_out, multiplexer_14_out, multiplexer_15_out,
       multiplexer_16_out, or_1_out;
  wire [7:0] multiplexer_17_out;

  Multiplexer #(.enable("false")) multiplexer_1 (.in0(in_1[0]), .in1(1'b0), .out(multiplexer_1_out), .sel(in_2[0]));
  Multiplexer #(.enable("false")) multiplexer_2 (.in0(in_1[1]), .in1(in_1[0]), .out(multiplexer_2_out), .sel(in_2[0]));
  Multiplexer #(.enable("false")) multiplexer_3 (.in0(in_1[2]), .in1(in_1[1]), .out(multiplexer_3_out), .sel(in_2[0]));
  Multiplexer #(.enable("false")) multiplexer_4 (.in0(in_1[3]), .in1(in_1[2]), .out(multiplexer_4_out), .sel(in_2[0]));
  Multiplexer #(.enable("false")) multiplexer_5 (.in0(in_1[4]), .in1(in_1[3]), .out(multiplexer_5_out), .sel(in_2[0]));
  Multiplexer #(.enable("false")) multiplexer_6 (.in0(in_1[5]), .in1(in_1[4]), .out(multiplexer_6_out), .sel(in_2[0]));
  Multiplexer #(.enable("false")) multiplexer_7 (.in0(in_1[6]), .in1(in_1[5]), .out(multiplexer_7_out), .sel(in_2[0]));
  Multiplexer #(.enable("false")) multiplexer_8 (.in0(in_1[7]), .in1(in_1[6]), .out(multiplexer_8_out), .sel(in_2[0]));
  Multiplexer #(.enable("false")) multiplexer_9 (
    .in0(multiplexer_1_out), .in1(1'b0), .out(multiplexer_9_out), .sel(in_2[1]));
  Multiplexer #(.enable("false")) multiplexer_10 (
    .in0(multiplexer_2_out), .in1(1'b0), .out(multiplexer_10_out), .sel(in_2[1]));
  Multiplexer #(.enable("false")) multiplexer_11 (
    .in0(multiplexer_3_out), .in1(multiplexer_1_out), .out(multiplexer_11_out), .sel(in_2[1]));
  Multiplexer #(.enable("false")) multiplexer_12 (
    .in0(multiplexer_4_out), .in1(multiplexer_2_out), .out(multiplexer_12_out), .sel(in_2[1]));
  Multiplexer #(.enable("false")) multiplexer_13 (
    .in0(multiplexer_5_out), .in1(multiplexer_3_out), .out(multiplexer_13_out), .sel(in_2[1]));
  Multiplexer #(.enable("false")) multiplexer_14 (
    .in0(multiplexer_6_out), .in1(multiplexer_4_out), .out(multiplexer_14_out), .sel(in_2[1]));
  Multiplexer #(.enable("false")) multiplexer_15 (
    .in0(multiplexer_7_out), .in1(multiplexer_5_out), .out(multiplexer_15_out), .sel(in_2[1]));
  Multiplexer #(.enable("false")) multiplexer_16 (
    .in0(multiplexer_8_out), .in1(multiplexer_6_out), .out(multiplexer_16_out), .sel(in_2[1]));
  Multiplexer #(.enable("false")) multiplexer_17 (
    .in0(multiplexer_9_out), .in1(1'b0), .out(multiplexer_17_out[0]), .sel(in_2[2]));
  Multiplexer #(.enable("false")) multiplexer_18 (
    .in0(multiplexer_10_out), .in1(1'b0), .out(multiplexer_17_out[1]), .sel(in_2[2]));
  Multiplexer #(.enable("false")) multiplexer_19 (
    .in0(multiplexer_11_out), .in1(1'b0), .out(multiplexer_17_out[2]), .sel(in_2[2]));
  Multiplexer #(.enable("false")) multiplexer_20 (
    .in0(multiplexer_12_out), .in1(1'b0), .out(multiplexer_17_out[3]), .sel(in_2[2]));
  Multiplexer #(.enable("false")) multiplexer_21 (
    .in0(multiplexer_13_out), .in1(multiplexer_9_out), .out(multiplexer_17_out[4]), .sel(in_2[2]));
  Multiplexer #(.enable("false")) multiplexer_22 (
    .in0(multiplexer_14_out), .in1(multiplexer_10_out), .out(multiplexer_17_out[5]), .sel(in_2[2]));
  Multiplexer #(.enable("false")) multiplexer_23 (
    .in0(multiplexer_15_out), .in1(multiplexer_11_out), .out(multiplexer_17_out[6]), .sel(in_2[2]));
  Multiplexer #(.enable("false")) multiplexer_24 (
    .in0(multiplexer_16_out), .in1(multiplexer_12_out), .out(multiplexer_17_out[7]), .sel(in_2[2]));
  or or_1 (or_1_out, in_2[3], in_2[4], in_2[5], in_2[6], in_2[7]);
  Multiplexer #(.enable("false"), .width(8)) multiplexer_25 (
    .in0(multiplexer_17_out), .in1({8{1'b0}}), .out(Out), .sel(or_1_out));

  // Notes on the sheet:
  //   Input
  //   Shift
endmodule
