// Logisim project teste.circ as structural Verilog: 1 circuit, main circuit main
module main (
  input  in_1,
  input  in_2,
  output [7:0] out_3
);

  wire CLK, clock_1_out;
  wire [7:0] adder_1_out, PC, ram_1_dout, register_1_q;
  wire [13:0] rom_1_data;

  Register register_1 (.D(adder_1_out), .en(1'b1), .clk(clock_1_out), .Q(register_1_q), .clr(in_1));
  Clock clock_1 (.out(clock_1_out));
  Adder adder_1 (.a(register_1_q), .b(8'h1), .out(adder_1_out));  // open: cin, cout
  RAM #(.asyncread("true")) ram_1 (.addr(PC), .we(1'b0), .oe(1'b1), .clk(CLK), .dout(ram_1_dout));  // open: din
  ROM #(.addrWidth(4), .dataWidth(14)) rom_1 (.addr(out_3[7:4]), .data(rom_1_data));

  // Notes on the sheet:
  //   Memória de Instruções
  //   contents of rom_1 (hex, n*v repeats v):
  //   100 200 40 80 2030 8 2400 3800 2800 2000 2001 2002 2003 2004 2005 2006
  //   Memória de Controle
endmodule
