// Logisim project SaguiRaboLongo.circ as structural Verilog: 6 circuits, main circuit main
module main (
  input  in_1
);

  wire and_1_out, and_2_out, BR_IMM, BR_REG, CLK, JI, JR, M_RD, M_REG, M_WR, MOVH, MOVHL, MOVL, NOP_BRJ,
       NOP_SLM, NOP_ULA_1, NOP_ULA_2, nor_1_out, nor_2_out, not_3_out, not_4_out, or_1_out, RaZero, RW_0,
       RW_1, RW_2;
  wire [1:0] multiplexer_3_out, multiplexer_4_out;
  wire [2:0] SEL_ULA_1, SEL_ULA_2;
  wire [3:0] Imm, IMM_MOV, OPCODE_BRJ, OPCODE_LSM, ram_1_dout, ram_1_dout_3, rom_2_data;
  wire [3:3] ram_1_dout_2, ram_1_dout_4;
  wire [6:0] rom_1_data;
  wire [7:0] adder_1_out, adder_2_out, bit_extender_1_out, br_1_out_29, br_1_out_30, br_1_out_31,
       br_1_out_32, br_1_out_33, br_1_r_ra, br_1_r_rb, IN_0, movehighlowbox_1_move_high,
       movehighlowbox_1_move_low, multiplexer_1_out, multiplexer_2_out, multiplexer_6_out, multiplexer_7_out,
       OUT_ULA_1, OUT_ULA_2, PC, ram_2_dout, Rrb;
  wire [31:0] REGS;

  // Probe on PC
  // Probe on PC
  // Probe on REGS[7:0]
  // Probe on REGS[7:0]
  // Probe on REGS[15:8]
  // Probe on REGS[15:8]
  // Probe on REGS[23:16]
  // Probe on REGS[23:16]
  // Probe on REGS[31:24]
  // Probe on REGS[31:24]
  Clock clock_1 (.out(CLK));
  // Probe on PC
  // Probe on REGS[7:0]
  // Probe on REGS[15:8]
  // Probe on REGS[23:16]
  // Probe on REGS[31:24]
  RAM #(.asyncread("true"), .dataWidth(32)) ram_1 (
    .addr(PC), .we(1'b0), .oe(1'b1), .clk(CLK),
    .dout({OPCODE_LSM, IMM_MOV, OPCODE_BRJ, Imm, ram_1_dout_4[3], SEL_ULA_1, ram_1_dout_3, ram_1_dout_2[3], SEL_ULA_2, ram_1_dout}));  // open: din
  Register register_1 (.D(multiplexer_2_out), .en(1'b1), .clk(CLK), .Q(PC), .clr(in_1));
  Adder adder_1 (.a(PC), .b(8'h1), .out(adder_1_out));  // open: cin, cout
  and and_1 (and_1_out, BR_REG, RaZero);
  nor nor_1 (nor_1_out, JR, and_1_out);
  assign bit_extender_1_out = {{4{1'b0}}, Imm};  // Bit_Extender bit_extender_1
  Adder adder_2 (.a(PC), .b(bit_extender_1_out), .out(adder_2_out));  // open: cin, cout
  and and_2 (and_2_out, BR_IMM, RaZero);
  Multiplexer #(.enable("false"), .width(8)) multiplexer_1 (
    .in0(adder_2_out), .in1(adder_1_out), .out(multiplexer_1_out), .sel(nor_2_out));
  nor nor_2 (nor_2_out, JI, and_2_out);
  Multiplexer #(.enable("false"), .width(8)) multiplexer_2 (
    .in0(Rrb), .in1(multiplexer_1_out), .out(multiplexer_2_out), .sel(nor_1_out));
  Comparator #(.mode("unsigned"), .width(4)) comparator_1 (.a(OPCODE_LSM), .b(4'b1111), .eq(NOP_SLM));  // open: gt, lt
  Comparator #(.mode("unsigned"), .width(4)) comparator_2 (
    .a({ram_1_dout_4[3], SEL_ULA_1}), .b(4'b1111), .eq(NOP_ULA_1));  // open: gt, lt
  Comparator #(.mode("unsigned"), .width(4)) comparator_3 (
    .a({ram_1_dout_2[3], SEL_ULA_2}), .b(4'b1111), .eq(NOP_ULA_2));  // open: gt, lt
  Comparator #(.mode("unsigned"), .width(4)) comparator_4 (.a(OPCODE_BRJ), .b(4'b1111), .eq(NOP_BRJ));  // open: gt, lt
  not not_1 (RW_1, NOP_ULA_1);
  not not_2 (RW_2, NOP_ULA_2);
  Multiplexer #(.enable("false"), .width(2)) multiplexer_3 (
    .in0(IMM_MOV[3:2]), .in1(2'b00), .out(multiplexer_3_out), .sel(MOVHL));
  Multiplexer #(.enable("false"), .width(2)) multiplexer_4 (
    .in0(Imm[3:2]), .in1(2'b00), .out(multiplexer_4_out), .sel(BR_IMM));
  ROM #(.addrWidth(2), .dataWidth(7)) rom_1 (.addr(OPCODE_LSM[1:0]), .data(rom_1_data));
  BR br_1 (
    .out_23(REGS[7:0]), .out_24(REGS[15:8]), .out_25(REGS[23:16]), .out_26(REGS[31:24]),
    .out_33(br_1_out_33), .out_34(Rrb), .R_ra(br_1_r_ra), .R_rb(br_1_r_rb), .out_29(br_1_out_29),
    .out_30(br_1_out_30), .out_31(br_1_out_31), .out_32(br_1_out_32), .ResetGeral(in_1),
    .rb_2(ram_1_dout[1:0]), .ra_3(multiplexer_4_out), .rb_3(Imm[1:0]), .ra_0(multiplexer_3_out),
    .rb_0(IMM_MOV[1:0]), .ra_1(ram_1_dout_3[3:2]), .rb_1(ram_1_dout_3[1:0]), .ra_2(ram_1_dout[3:2]),
    .in_4(ram_1_dout[3:2]), .in_13(ram_1_dout[3:2]), .U1(OUT_ULA_2), .in_10(RW_2), .in_5(ram_1_dout_3[3:2]),
    .in_14(ram_1_dout_3[3:2]), .in_2(OUT_ULA_1), .in_11(RW_1), .in_1(IN_0), .in_6(multiplexer_3_out),
    .in_15(multiplexer_3_out), .in_12(RW_0), .CLK(CLK));
  not not_3 (not_3_out, NOP_SLM);
  Comparator comparator_5 (.a({8{1'b0}}), .b(br_1_out_33), .eq(RaZero));  // open: gt, lt
  and and_3 (MOVL, not_3_out, rom_1_data[0]);
  and and_4 (MOVH, not_3_out, rom_1_data[1]);
  and and_5 (MOVHL, not_3_out, rom_1_data[2]);
  and and_6 (M_WR, not_3_out, rom_1_data[3]);
  and and_7 (M_RD, not_3_out, rom_1_data[4]);
  and and_8 (M_REG, not_3_out, rom_1_data[5]);
  and and_9 (RW_0, not_3_out, rom_1_data[6]);
  ROM #(.addrWidth(2), .dataWidth(4)) rom_2 (.addr(OPCODE_BRJ[1:0]), .data(rom_2_data));
  RAM #(.asyncread("true")) ram_2 (
    .addr(br_1_r_rb), .we(M_WR), .oe(M_RD), .clk(CLK), .din(br_1_r_ra), .dout(ram_2_dout));
  not not_4 (not_4_out, NOP_BRJ);
  ULA ula_1 (.\Saída_ULA (OUT_ULA_1), .in_1(br_1_out_29), .in_2(br_1_out_30), .ULA_src(SEL_ULA_1));
  ULA ula_2 (.\Saída_ULA (OUT_ULA_2), .in_1(br_1_out_31), .in_2(br_1_out_32), .ULA_src(SEL_ULA_2));
  and and_10 (JI, not_4_out, rom_2_data[0]);
  and and_11 (JR, not_4_out, rom_2_data[1]);
  and and_12 (BR_IMM, not_4_out, rom_2_data[2]);
  and and_13 (BR_REG, not_4_out, rom_2_data[3]);
  Multiplexer #(.enable("false"), .width(8)) multiplexer_5 (
    .in0(multiplexer_6_out), .in1({8{1'b0}}), .out(IN_0), .sel(or_1_out));
  or or_1 (or_1_out, NOP_SLM, M_WR);
  Multiplexer #(.enable("false"), .width(8)) multiplexer_6 (
    .in0(multiplexer_7_out), .in1(ram_2_dout), .out(multiplexer_6_out), .sel(M_REG));
  Multiplexer #(.enable("false"), .width(8)) multiplexer_7 (
    .in0(movehighlowbox_1_move_low), .in1(movehighlowbox_1_move_high), .out(multiplexer_7_out), .sel(MOVH));
  MoveHighLowBox movehighlowbox_1 (
    .Move_HIGH(movehighlowbox_1_move_high), .Move_LOW(movehighlowbox_1_move_low), .Imm(IMM_MOV),
    .in_2(br_1_r_ra));

  // Other names for the same wires on the sheet: ResetGeral = in_1

  // Notes on the sheet:
  //   R[0]
  //   R[1]
  //   R[2]
  //   R[3]
  //   Memória de Instruções
  //   ULA_2
  //   ULA_1
  //   BR/JMP
  //   LD/ST/MV
  //   PC
  //   PC + 1
  //   PC + Imm
  //   contents of rom_1 (hex, n*v repeats v):
  //   70 8 46 45
  //   LD/ST/MV
  //   BR/JMP
  //   contents of rom_2 (hex, n*v repeats v):
  //   8 4 2 1
endmodule

module ULA (
  input  [7:0] in_1,
  input  [7:0] in_2,
  input  [2:0] ULA_src,
  output [7:0] \Saída_ULA 
);

  wire [7:0] adder_1_out, and_1_out, lbs_1_out, not_1_out, or_1_out, rbs_1_out, subtractor_1_out;

  Adder adder_1 (.a(in_1), .b(in_2), .out(adder_1_out));  // open: cin, cout
  Subtractor subtractor_1 (.a(in_1), .b(in_2), .out(subtractor_1_out));  // open: bin, bout
  assign and_1_out = in_1 & in_2;  // AND_Gate and_1, 8 bits wide
  assign or_1_out = in_1 | in_2;  // OR_Gate or_1, 8 bits wide
  assign not_1_out = ~in_2;  // NOT_Gate not_1, 8 bits wide
  LBS lbs_1 (.Out(lbs_1_out), .in_1(in_1), .in_2(in_2));
  RBS rbs_1 (.Out(rbs_1_out), .in_1(in_1), .in_2(in_2));
  Multiplexer #(.enable("false"), .select(3), .width(8)) multiplexer_1 (
    .in0(adder_1_out), .in1(subtractor_1_out), .in2(and_1_out), .in3(or_1_out), .in4(not_1_out),
    .in5(lbs_1_out), .in6(rbs_1_out), .in7({8{1'b0}}), .out(\Saída_ULA ), .sel(ULA_src));

  // Other names for the same wires on the sheet: Rra[7:0] = in_1; Rrb[7:0] = in_2

  // Notes on the sheet:
  //   R[ra]
  //   R[rb]
  //   ULA
endmodule

module MoveHighLowBox (
  input  [3:0] Imm,
  input  [7:0] in_2,
  output [7:0] Move_HIGH,
  output [7:0] Move_LOW
);


  assign Move_HIGH = {Imm, in_2[3:0]};
  assign Move_LOW = {in_2[7:4], Imm};

  // Notes on the sheet:
  //   Registrador
endmodule

module RBS (
  input  [7:0] in_1,
  input  [7:0] in_2,
  output [7:0] Out
);

  wire multiplexer_1_out, multiplexer_2_out, multiplexer_3_out, multiplexer_4_out, multiplexer_5_out,
       multiplexer_6_out, multiplexer_7_out, multiplexer_8_out, multiplexer_9_out, multiplexer_10_out,
       multiplexer_11_out, multiplexer_12_out, multiplexer_13_out, multiplexer_14_out, multiplexer_15_out,
       multiplexer_16_out, or_1_out;
  wire [7:0] multiplexer_17_out;

  Multiplexer #(.enable("false")) multiplexer_1 (.in0(in_1[0]), .in1(in_1[1]), .out(multiplexer_1_out), .sel(in_2[0]));
  Multiplexer #(.enable("false")) multiplexer_2 (.in0(in_1[1]), .in1(in_1[2]), .out(multiplexer_2_out), .sel(in_2[0]));
  Multiplexer #(.enable("false")) multiplexer_3 (.in0(in_1[2]), .in1(in_1[3]), .out(multiplexer_3_out), .sel(in_2[0]));
  Multiplexer #(.enable("false")) multiplexer_4 (.in0(in_1[3]), .in1(in_1[4]), .out(multiplexer_4_out), .sel(in_2[0]));
  Multiplexer #(.enable("false")) multiplexer_5 (.in0(in_1[4]), .in1(in_1[5]), .out(multiplexer_5_out), .sel(in_2[0]));
  Multiplexer #(.enable("false")) multiplexer_6 (.in0(in_1[5]), .in1(in_1[6]), .out(multiplexer_6_out), .sel(in_2[0]));
  Multiplexer #(.enable("false")) multiplexer_7 (.in0(in_1[6]), .in1(in_1[7]), .out(multiplexer_7_out), .sel(in_2[0]));
  Multiplexer #(.enable("false")) multiplexer_8 (.in0(in_1[7]), .in1(1'b0), .out(multiplexer_8_out), .sel(in_2[0]));
  Multiplexer #(.enable("false")) multiplexer_9 (
    .in0(multiplexer_1_out), .in1(multiplexer_3_out), .out(multiplexer_9_out), .sel(in_2[1]));
  Multiplexer #(.enable("false")) multiplexer_10 (
    .in0(multiplexer_2_out), .in1(multiplexer_4_out), .out(multiplexer_10_out), .sel(in_2[1]));
  Multiplexer #(.enable("false")) multiplexer_11 (
    .in0(multiplexer_3_out), .in1(multiplexer_5_out), .out(multiplexer_11_out), .sel(in_2[1]));
  Multiplexer #(.enable("false")) multiplexer_12 (
    .in0(multiplexer_4_out), .in1(multiplexer_6_out), .out(multiplexer_12_out), .sel(in_2[1]));
  Multiplexer #(.enable("false")) multiplexer_13 (
    .in0(multiplexer_5_out), .in1(multiplexer_7_out), .out(multiplexer_13_out), .sel(in_2[1]));
  Multiplexer #(.enable("false")) multiplexer_14 (
    .in0(multiplexer_6_out), .in1(multiplexer_8_out), .out(multiplexer_14_out), .sel(in_2[1]));
  Multiplexer #(.enable("false")) multiplexer_15 (
    .in0(multiplexer_7_out), .in1(1'b0), .out(multiplexer_15_out), .sel(in_2[1]));
  Multiplexer #(.enable("false")) multiplexer_16 (
    .in0(multiplexer_8_out), .in1(1'b0), .out(multiplexer_16_out), .sel(in_2[1]));
  Multiplexer #(.enable("false")) multiplexer_17 (
    .in0(multiplexer_9_out), .in1(multiplexer_13_out), .out(multiplexer_17_out[0]), .sel(in_2[2]));
  Multiplexer #(.enable("false")) multiplexer_18 (
    .in0(multiplexer_10_out), .in1(multiplexer_14_out), .out(multiplexer_17_out[1]), .sel(in_2[2]));
  Multiplexer #(.enable("false")) multiplexer_19 (
    .in0(multiplexer_11_out), .in1(multiplexer_15_out), .out(multiplexer_17_out[2]), .sel(in_2[2]));
  Multiplexer #(.enable("false")) multiplexer_20 (
    .in0(multiplexer_12_out), .in1(multiplexer_16_out), .out(multiplexer_17_out[3]), .sel(in_2[2]));
  Multiplexer #(.enable("false")) multiplexer_21 (
    .in0(multiplexer_13_out), .in1(1'b0), .out(multiplexer_17_out[4]), .sel(in_2[2]));
  Multiplexer #(.enable("false")) multiplexer_22 (
    .in0(multiplexer_14_out), .in1(1'b0), .out(multiplexer_17_out[5]), .sel(in_2[2]));
  Multiplexer #(.enable("false")) multiplexer_23 (
    .in0(multiplexer_15_out), .in1(1'b0), .out(multiplexer_17_out[6]), .sel(in_2[2]));
  Multiplexer #(.enable("false")) multiplexer_24 (
    .in0(multiplexer_16_out), .in1(1'b0), .out(multiplexer_17_out[7]), .sel(in_2[2]));
  or or_1 (or_1_out, in_2[3], in_2[4], in_2[5], in_2[6], in_2[7]);
  Multiplexer #(.enable("false"), .width(8)) multiplexer_25 (
    .in0(multiplexer_17_out), .in1({8{1'b0}}), .out(Out), .sel(or_1_out));

  // Notes on the sheet:
  //   Input
  //   Shift
endmodule

module LBS (
  input  [7:0] in_1,
  input  [7:0] in_2,
  output [7:0] Out
);

  wire multiplexer_1_out, multiplexer_2_out, multiplexer_3_out, multiplexer_4_out, multiplexer_5_out,
       multiplexer_6_out, multiplexer_7_out, multiplexer_8_out, multiplexer_9_out, multiplexer_10_out,
       multiplexer_11_out, multiplexer_12_out, multiplexer_13_out, multiplexer_14_out, multiplexer_15_out,
       multiplexer_16_out, or_1_out;
  wire [7:0] multiplexer_17_out;

  Multiplexer #(.enable("false")) multiplexer_1 (.in0(in_1[0]), .in1(1'b0), .out(multiplexer_1_out), .sel(in_2[0]));
  Multiplexer #(.enable("false")) multiplexer_2 (.in0(in_1[1]), .in1(in_1[0]), .out(multiplexer_2_out), .sel(in_2[0]));
  Multiplexer #(.enable("false")) multiplexer_3 (.in0(in_1[2]), .in1(in_1[1]), .out(multiplexer_3_out), .sel(in_2[0]));
  Multiplexer #(.enable("false")) multiplexer_4 (.in0(in_1[3]), .in1(in_1[2]), .out(multiplexer_4_out), .sel(in_2[0]));
  Multiplexer #(.enable("false")) multiplexer_5 (.in0(in_1[4]), .in1(in_1[3]), .out(multiplexer_5_out), .sel(in_2[0]));
  Multiplexer #(.enable("false")) multiplexer_6 (.in0(in_1[5]), .in1(in_1[4]), .out(multiplexer_6_out), .sel(in_2[0]));
  Multiplexer #(.enable("false")) multiplexer_7 (.in0(in_1[6]), .in1(in_1[5]), .out(multiplexer_7_out), .sel(in_2[0]));
  Multiplexer #(.enable("false")) multiplexer_8 (.in0(in_1[7]), .in1(in_1[6]), .out(multiplexer_8_out), .sel(in_2[0]));
  Multiplexer #(.enable("false")) multiplexer_9 (
    .in0(multiplexer_1_out), .in1(1'b0), .out(multiplexer_9_out), .sel(in_2[1]));
  Multiplexer #(.enable("false")) multiplexer_10 (
    .in0(multiplexer_2_out), .in1(1'b0), .out(multiplexer_10_out), .sel(in_2[1]));
  Multiplexer #(.enable("false")) multiplexer_11 (
    .in0(multiplexer_3_out), .in1(multiplexer_1_out), .out(multiplexer_11_out), .sel(in_2[1]));
  Multiplexer #(.enable("false")) multiplexer_12 (
    .in0(multiplexer_4_out), .in1(multiplexer_2_out), .out(multiplexer_12_out), .sel(in_2[1]));
  Multiplexer #(.enable("false")) multiplexer_13 (
    .in0(multiplexer_5_out), .in1(multiplexer_3_out), .out(multiplexer_13_out), .sel(in_2[1]));
  Multiplexer #(.enable("false")) multiplexer_14 (
    .in0(multiplexer_6_out), .in1(multiplexer_4_out), .out(multiplexer_14_out), .sel(in_2[1]));
  Multiplexer #(.enable("false")) multiplexer_15 (
    .in0(multiplexer_7_out), .in1(multiplexer_5_out), .out(multiplexer_15_out), .sel(in_2[1]));
  Multiplexer #(.enable("false")) multiplexer_16 (
    .in0(multiplexer_8_out), .in1(multiplexer_6_out), .out(multiplexer_16_out), .sel(in_2[1]));
  Multiplexer #(.enable("false")) multiplexer_17 (
    .in0(multiplexer_9_out), .in1(1'b0), .out(multiplexer_17_out[0]), .sel(in_2[2]));
  Multiplexer #(.enable("false")) multiplexer_18 (
    .in0(multiplexer_10_out), .in1(1'b0), .out(multiplexer_17_out[1]), .sel(in_2[2]));
  Multiplexer #(.enable("false")) multiplexer_19 (
    .in0(multiplexer_11_out), .in1(1'b0), .out(multiplexer_17_out[2]), .sel(in_2[2]));
  Multiplexer #(.enable("false")) multiplexer_20 (
    .in0(multiplexer_12_out), .in1(1'b0), .out(multiplexer_17_out[3]), .sel(in_2[2]));
  Multiplexer #(.enable("false")) multiplexer_21 (
    .in0(multiplexer_13_out), .in1(multiplexer_9_out), .out(multiplexer_17_out[4]), .sel(in_2[2]));
  Multiplexer #(.enable("false")) multiplexer_22 (
    .in0(multiplexer_14_out), .in1(multiplexer_10_out), .out(multiplexer_17_out[5]), .sel(in_2[2]));
  Multiplexer #(.enable("false")) multiplexer_23 (
    .in0(multiplexer_15_out), .in1(multiplexer_11_out), .out(multiplexer_17_out[6]), .sel(in_2[2]));
  Multiplexer #(.enable("false")) multiplexer_24 (
    .in0(multiplexer_16_out), .in1(multiplexer_12_out), .out(multiplexer_17_out[7]), .sel(in_2[2]));
  or or_1 (or_1_out, in_2[3], in_2[4], in_2[5], in_2[6], in_2[7]);
  Multiplexer #(.enable("false"), .width(8)) multiplexer_25 (
    .in0(multiplexer_17_out), .in1({8{1'b0}}), .out(Out), .sel(or_1_out));

  // Notes on the sheet:
  //   Input
  //   Shift
endmodule

module BR (
  input  [7:0] in_1,
  input  [7:0] in_2,
  input  [7:0] U1,
  input  [1:0] in_4,
  input  [1:0] in_5,
  input  [1:0] in_6,
  input  [1:0] ra_0,
  input  [1:0] rb_0,
  input  [1:0] ra_1,
  input  in_10,
  input  in_11,
  input  in_12,
  input  [1:0] in_13,
  input  [1:0] in_14,
  input  [1:0] in_15,
  input  [1:0] rb_1,
  input  CLK,
  input  ResetGeral,
  input  [1:0] ra_2,
  input  [1:0] rb_2,
  input  [1:0] ra_3,
  input  [1:0] rb_3,
  output [7:0] out_23,
  output [7:0] out_24,
  output [7:0] out_25,
  output [7:0] out_26,
  output [7:0] R_ra,
  output [7:0] R_rb,
  output [7:0] out_29,
  output [7:0] out_30,
  output [7:0] out_31,
  output [7:0] out_32,
  output [7:0] out_33,
  output [7:0] out_34
);

  wire demultiplexer_3_out0, demultiplexer_3_out1, demultiplexer_3_out2, demultiplexer_3_out3,
       demultiplexer_4_out0, demultiplexer_4_out1, demultiplexer_4_out2, demultiplexer_4_out3,
       demultiplexer_6_out0, demultiplexer_6_out1, demultiplexer_6_out2, demultiplexer_6_out3, or_5_out,
       or_6_out, or_7_out, or_8_out;
  wire [7:0] demultiplexer_1_out0, demultiplexer_1_out1, demultiplexer_1_out2, demultiplexer_1_out3,
       demultiplexer_2_out0, demultiplexer_2_out1, demultiplexer_2_out2, demultiplexer_2_out3,
       demultiplexer_5_out0, demultiplexer_5_out1, demultiplexer_5_out2, demultiplexer_5_out3, or_1_out,
       or_2_out, or_3_out, or_4_out;

  Demultiplexer #(.enable("false"), .select(2), .width(8)) demultiplexer_1 (
    .out0(demultiplexer_1_out0), .out1(demultiplexer_1_out1), .out2(demultiplexer_1_out2),
    .out3(demultiplexer_1_out3), .in(U1), .sel(in_4));
  Demultiplexer #(.enable("false"), .select(2), .width(8)) demultiplexer_2 (
    .out0(demultiplexer_2_out0), .out1(demultiplexer_2_out1), .out2(demultiplexer_2_out2),
    .out3(demultiplexer_2_out3), .in(in_2), .sel(in_5));
  Demultiplexer #(.enable("false"), .select(2)) demultiplexer_3 (
    .out0(demultiplexer_3_out0), .out1(demultiplexer_3_out1), .out2(demultiplexer_3_out2),
    .out3(demultiplexer_3_out3), .in(in_10), .sel(in_13));
  Demultiplexer #(.enable("false"), .select(2)) demultiplexer_4 (
    .out0(demultiplexer_4_out0), .out1(demultiplexer_4_out1), .out2(demultiplexer_4_out2),
    .out3(demultiplexer_4_out3), .in(in_11), .sel(in_14));
  Demultiplexer #(.enable("false"), .select(2), .width(8)) demultiplexer_5 (
    .out0(demultiplexer_5_out0), .out1(demultiplexer_5_out1), .out2(demultiplexer_5_out2),
    .out3(demultiplexer_5_out3), .in(in_1), .sel(in_6));
  Demultiplexer #(.enable("false"), .select(2)) demultiplexer_6 (
    .out0(demultiplexer_6_out0), .out1(demultiplexer_6_out1), .out2(demultiplexer_6_out2),
    .out3(demultiplexer_6_out3), .in(in_12), .sel(in_15));
  assign or_1_out = demultiplexer_5_out0 | demultiplexer_2_out0 | demultiplexer_1_out0;  // OR_Gate or_1, 8 bits wide
  assign or_2_out = demultiplexer_5_out1 | demultiplexer_2_out1 | demultiplexer_1_out1;  // OR_Gate or_2, 8 bits wide
  assign or_3_out = demultiplexer_5_out2 | demultiplexer_2_out2 | demultiplexer_1_out2;  // OR_Gate or_3, 8 bits wide
  assign or_4_out = demultiplexer_5_out3 | demultiplexer_2_out3 | demultiplexer_1_out3;  // OR_Gate or_4, 8 bits wide
  or or_5 (or_5_out, demultiplexer_6_out3, demultiplexer_4_out3, demultiplexer_3_out3);
  or or_6 (or_6_out, demultiplexer_6_out2, demultiplexer_4_out2, demultiplexer_3_out2);
  or or_7 (or_7_out, demultiplexer_6_out1, demultiplexer_4_out1, demultiplexer_3_out1);
  or or_8 (or_8_out, demultiplexer_6_out0, demultiplexer_4_out0, demultiplexer_3_out0);
  Register register_1 (.D(or_1_out), .en(or_8_out), .clk(CLK), .Q(out_23), .clr(ResetGeral));
  Register register_2 (.D(or_2_out), .en(or_7_out), .clk(CLK), .Q(out_24), .clr(ResetGeral));
  Register register_3 (.D(or_3_out), .en(or_6_out), .clk(CLK), .Q(out_25), .clr(ResetGeral));
  Register register_4 (.D(or_4_out), .en(or_5_out), .clk(CLK), .Q(out_26), .clr(ResetGeral));
  Multiplexer #(.enable("false"), .select(2), .width(8)) multiplexer_1 (
    .in0(out_23), .in1(out_24), .in2(out_25), .in3(out_26), .out(R_ra), .sel(ra_0));
  Multiplexer #(.enable("false"), .select(2), .width(8)) multiplexer_2 (
    .in0(out_23), .in1(out_24), .in2(out_25), .in3(out_26), .out(R_rb), .sel(rb_0));
  Multiplexer #(.enable("false"), .select(2), .width(8)) multiplexer_3 (
    .in0(out_23), .in1(out_24), .in2(out_25), .in3(out_26), .out(out_29), .sel(ra_1));
  Multiplexer #(.enable("false"), .select(2), .width(8)) multiplexer_4 (
    .in0(out_23), .in1(out_24), .in2(out_25), .in3(out_26), .out(out_30), .sel(rb_1));
  Multiplexer #(.enable("false"), .select(2), .width(8)) multiplexer_5 (
    .in0(out_23), .in1(out_24), .in2(out_25), .in3(out_26), .out(out_31), .sel(ra_2));
  Multiplexer #(.enable("false"), .select(2), .width(8)) multiplexer_6 (
    .in0(out_23), .in1(out_24), .in2(out_25), .in3(out_26), .out(out_32), .sel(rb_2));
  Multiplexer #(.enable("false"), .select(2), .width(8)) multiplexer_7 (
    .in0(out_23), .in1(out_24), .in2(out_25), .in3(out_26), .out(out_33), .sel(ra_3));
  Multiplexer #(.enable("false"), .select(2), .width(8)) multiplexer_8 (
    .in0(out_23), .in1(out_24), .in2(out_25), .in3(out_26), .out(out_34), .sel(rb_3));

  // Notes on the sheet:
  //   ULA 2
  //   LD/ST/MOV
  //   ULA 1
  //   U2
  //   ULA 2
  //   ULA 1
  //   LSM
  //   ST/LD/MOV
  //   R0
  //   R1
  //   R2
  //   R3
  //   R[a]
  //   R[rb]
  //   R[0]
  //   R[1]
  //   R[2]
  //   R[3]
endmodule
